# Fritzing sketch TempRelayUno9V (saved by Fritzing 0.9.2b)

parts:
  Part3 = Arduino Uno (Rev3) - ICSP
  Part4 = Digital Temperature Sensor Breakout - TMP102
  U1 = RELAY [package=relay-jzc]
  BC338 = TRANSISTOR_NPN_2 [package=to-92]
  part = Resistor [tolerance=±5% resistance=1k package="1206 [SMD]"]
  D3 = Rectifier Diode [part_number=Rectifier package="Melf DO-213 AA [SMD]"]
  part_2 = Battery block 9V

nets:
  N1: Part3.A4/SDA, Part4.SDA
  N2: Part3.A5/SCL, Part4.SCL
  N3: Part3.D4, part.Pin_1
  N4: Part3.3V3, Part4.V+
  N5: Part3.5V, U1.COIL2, D3.cathode
  GND: Part3.GND, Part4.GND, Part4.ADD0, BC338.E, part_2.-
  N6: Part3.VIN, part_2.+
  N7: U1.COIL1, BC338.C, D3.anode
  N8: BC338.B, part.Pin_0
